# Fritzing sketch Schalt_Steckplan_1_3 (saved by Fritzing 0.9.9b)
breadboards: 1

parts:
  Bauteil1 = Arduino Uno (Rev3)
  LED1 = LED - 5mm [color="Red (633nm)" current=0.030 package="5 mm [THT]"]
  LED2 = LED - 5mm [color="Red (633nm)" current=0.030 package="5 mm [THT]"]
  LED3 = LED - 5mm [color="Red (633nm)" current=0.030 package="5 mm [THT]"]
  LED4 = LED - 5mm [color="Red (633nm)" current=0.030 package="5 mm [THT]"]
  LED5 = LED - 5mm [color="Red (633nm)" current=0.030 package="5 mm [THT]"]
  LED6 = LED - 5mm [color="Red (633nm)" current=0.030 package="5 mm [THT]"]
  LED7 = LED - 5mm [color="Red (633nm)" current=0.030 package="5 mm [THT]"]
  LED8 = LED - 5mm [color="Red (633nm)" current=0.030 package="5 mm [THT]"]
  R1 = Resistor [tolerance=±5% power=0.25 resistance=220 package=THT]
  R2 = Resistor [tolerance=±5% power=0.25 resistance=220 package=THT]
  R3 = Resistor [tolerance=±5% power=0.25 resistance=220 package=THT]
  R4 = Resistor [tolerance=±5% power=0.25 resistance=220 package=THT]
  R5 = Resistor [tolerance=±5% power=0.25 resistance=220 package=THT]
  R6 = Resistor [tolerance=±5% power=0.25 resistance=220 package=THT]
  R7 = Resistor [tolerance=±5% power=0.25 resistance=220 package=THT]
  R8 = Resistor [tolerance=±5% power=0.25 resistance=220 package=THT]
  R9 = Resistor [tolerance=±5% power=0.25 resistance=220 package=THT]
  S1 = Pushbutton [package="[THT]"]

nets (from the schematic view):
  N1: Bauteil1.A0, S1.Pin_1, S1.Pin_2
  N2: Bauteil1.D8, R5.Pin_1
  N3: Bauteil1.D9_PWM, R4.Pin_1
  N4: Bauteil1.D10_PWM/SS, R3.Pin_1
  N5: Bauteil1.D11_PWM/MOSI, R2.Pin_1
  N6: Bauteil1.D12/MISO, R1.Pin_1
  N7: Bauteil1.GND, LED2.cathode
  N8: Bauteil1.D5_PWM, R8.Pin_1
  N9: Bauteil1.D6_PWM, R7.Pin_1
  N10: Bauteil1.D7, R6.Pin_1
  N11: LED1.anode, R4.Pin_0
  N12: LED2.anode, R1.Pin_0
  N13: LED3.anode, R2.Pin_0
  N14: LED4.anode, R3.Pin_0
  N15: LED5.anode, R5.Pin_0
  N16: LED6.anode, R6.Pin_0
  N17: LED7.anode, R7.Pin_0
  N18: LED8.cathode, R9.Pin_1
  N19: LED8.anode, R8.Pin_0
  N20: R9.Pin_0, S1.Pin_3, S1.Pin_4
